# Fritzing sketch ds18b20 (saved by Fritzing 0.9.4)

parts:
  Raspberry_Pi_B_rev1 = Raspberry Pi B rev1
  DS1 = DS18B20 1-Wire Temperature Sensor [part_number=DS18B20]
  R1 = Resistor [tolerance=±5% resistance=4.7k package=THT]
  DS2 = DS18B20 1-Wire Temperature Sensor [part_number=DS18B20]

nets:
  VDD: Raspberry_Pi_B_rev1.3V3, DS1.VDD, DS2.VDD
  GND: Raspberry_Pi_B_rev1.GND, DS1.GND, R1.Pin_0, DS2.GND
  N1: Raspberry_Pi_B_rev1.GPIO_4, DS1.DQ, R1.Pin_1, DS2.DQ
