# Fritzing sketch pcf8574 (saved by Fritzing 0.9.4)

parts:
  Raspberry_Pi_B_rev1 = Raspberry Pi B rev1
  U1 = PCF8574 [package="DIP16 [THT]"]

nets:
  5V: Raspberry_Pi_B_rev1.5V, U1.VCC
  N1: Raspberry_Pi_B_rev1.GPIO_0, U1.SDA
  N2: Raspberry_Pi_B_rev1.GPIO_1, U1.SCL
  GND: Raspberry_Pi_B_rev1.GND, U1.A0, U1.A1, U1.A2, U1.GND

notes:
  8 portów wejścia/wyjścia
