# Fritzing sketch relay (saved by Fritzing 0.9.4)

parts:
  Raspberry_Pi_B_rev1 = Raspberry Pi B rev1
  KY-1 = Keyes Relay [package=THT]
  LED3 = LEDs [package=led10mm]
  Part3 = Lilypad Battery Connect

nets:
  N1: Raspberry_Pi_B_rev1.GND, KY-1.ground
  N2: Raspberry_Pi_B_rev1.GPIO_4, KY-1.signal
  N3: Raspberry_Pi_B_rev1.5V, KY-1.power
  N4: KY-1.NC, Part3.+
  N5: KY-1.C, LED3.C
  N6: LED3.A, Part3.-

notes:
  Zasilanie 230V

custom parts:
  Keyes Relay: The Keyes 5V relay module is suitable for SCM development, home appliance control. It uses a 5V~12V TIL control signal which can control DC / AC signal.
  LEDs: LEDs Standard schematic elements and footprints for 5mm, 3mm, 1206, and 0603 sized LEDs. 5mm - Spark Fun Electronics SKU : COM-00529 (and others)
